// Logisim project Project.circ as structural Verilog: 13 circuits, main circuit ALU
module ALU (
  input  [15:0] A,
  input  [15:0] B,
  input  [2:0] Alu_OP,
  input  in_4,
  output [15:0] \output ,
  output ZeroFlag,
  output carry_out
);

  wire not_1_out;
  wire [15:0] adder_1_out, and_1_out, bit_extender_1_out, multiplexer_1_out, or_1_out, subtractor_1_out;

  assign and_1_out = A & B;  // AND_Gate and_1, 16 bits wide
  assign or_1_out = A | B;  // OR_Gate or_1, 16 bits wide
  Subtractor #(.width(16)) subtractor_1 (.a(A), .b(B), .out(subtractor_1_out), .bout(carry_out));  // open: bin
  Adder #(.width(16)) adder_1 (.a(A), .b(B), .out(adder_1_out));  // open: cin, cout
  not not_1 (not_1_out, carry_out);
  Multiplexer #(.width(16), .enable("false")) multiplexer_1 (
    .in0(B), .in1(A), .out(multiplexer_1_out), .sel(not_1_out));
  assign bit_extender_1_out = {{15{1'b0}}, carry_out};  // Bit_Extender bit_extender_1
  Multiplexer #(.select(3), .width(16)) multiplexer_2 (
    .in0({16{1'b0}}), .in1(bit_extender_1_out), .in2(subtractor_1_out), .in3(adder_1_out), .in4({16{1'b0}}),
    .in5(multiplexer_1_out), .in6(or_1_out), .in7(and_1_out), .out(\output ), .sel(Alu_OP), .en(in_4));
  or or_2 (ZeroFlag, \output [0], \output [1], \output [2], \output [3], \output [4], \output [5], \output [6], \output [7], \output [8], \output [9], \output [10], \output [11], \output [12], \output [13], \output [14], \output [15]);
endmodule

module Register (
  input  WR_en,
  input  [2:0] Decoder_sel,
  input  [15:0] BUS_W,
  input  [2:0] RA,
  input  [2:0] RB,
  input  CLK,
  output [15:0] BUS_A,
  output [15:0] BUS_B
);

  wire and_1_out, and_2_out, and_3_out, and_4_out, and_5_out, and_6_out, and_7_out, decoder_1_out1,
       decoder_1_out2, decoder_1_out3, decoder_1_out4, decoder_1_out5, decoder_1_out6, decoder_1_out7;
  wire [15:0] register_1_q, register_2_q, register_3_q, register_4_q, register_5_q, register_6_q,
       register_7_q;

  Decoder #(.select(3), .enable("false")) decoder_1 (
    .out1(decoder_1_out1), .out2(decoder_1_out2), .out3(decoder_1_out3), .out4(decoder_1_out4),
    .out5(decoder_1_out5), .out6(decoder_1_out6), .out7(decoder_1_out7), .sel(Decoder_sel));  // open: out0
  and and_1 (and_1_out, WR_en, decoder_1_out1);
  and and_2 (and_2_out, WR_en, decoder_1_out2);
  and and_3 (and_3_out, WR_en, decoder_1_out3);
  and and_4 (and_4_out, WR_en, decoder_1_out4);
  and and_5 (and_5_out, WR_en, decoder_1_out5);
  and and_6 (and_6_out, WR_en, decoder_1_out6);
  and and_7 (and_7_out, WR_en, decoder_1_out7);
  Register_part #(.width(16)) register_1 (.D(BUS_W), .en(and_1_out), .Q(register_1_q), .clk(CLK), .clr(1'b0));
  Register_part #(.width(16)) register_2 (.D(BUS_W), .en(and_2_out), .Q(register_2_q), .clk(CLK), .clr(1'b0));
  Register_part #(.width(16)) register_3 (.D(BUS_W), .en(and_3_out), .Q(register_3_q), .clk(CLK), .clr(1'b0));
  Register_part #(.width(16)) register_4 (.D(BUS_W), .en(and_4_out), .Q(register_4_q), .clk(CLK), .clr(1'b0));
  Register_part #(.width(16)) register_5 (.D(BUS_W), .en(and_5_out), .Q(register_5_q), .clk(CLK), .clr(1'b0));
  Register_part #(.width(16)) register_6 (.D(BUS_W), .en(and_6_out), .Q(register_6_q), .clk(CLK), .clr(1'b0));
  Register_part #(.width(16)) register_7 (.D(BUS_W), .en(and_7_out), .Q(register_7_q), .clk(CLK), .clr(1'b0));
  Multiplexer #(.select(3), .width(16)) multiplexer_1 (
    .in0({16{1'b0}}), .in1(register_1_q), .in2(register_2_q), .in3(register_3_q), .in4(register_4_q),
    .in5(register_5_q), .in6(register_6_q), .in7(register_7_q), .out(BUS_A), .sel(RA), .en(1'b1));
  Multiplexer #(.select(3), .width(16)) multiplexer_2 (
    .in0({16{1'b0}}), .in1(register_1_q), .in2(register_2_q), .in3(register_3_q), .in4(register_4_q),
    .in5(register_5_q), .in6(register_6_q), .in7(register_7_q), .out(BUS_B), .sel(RB), .en(1'b1));
endmodule

module Forwarding (
  input  EX_MEM_RegWrite,
  input  [2:0] EX_MEM_RegRd,
  input  MEM_WB_RegWrite,
  input  [2:0] ID_EX_RegRs,
  input  [2:0] ID_EX_RegRt,
  input  [2:0] MEM_WB_RegRd,
  output [1:0] ForwardA,
  output [1:0] ForwardB
);

  wire comparator_1_eq, comparator_2_eq, comparator_3_eq, comparator_4_eq, comparator_5_eq, comparator_6_eq;

  Comparator #(.width(3)) comparator_1 (.a(EX_MEM_RegRd), .b(ID_EX_RegRs), .eq(comparator_1_eq));  // open: gt, lt
  and and_1 (ForwardA[1], comparator_1_eq, ~comparator_4_eq, EX_MEM_RegWrite);  // AND_Gate
  and and_2 (ForwardB[1], comparator_2_eq, ~comparator_4_eq, EX_MEM_RegWrite);  // AND_Gate
  Comparator #(.width(3)) comparator_2 (.a(EX_MEM_RegRd), .b(ID_EX_RegRt), .eq(comparator_2_eq));  // open: gt, lt
  Comparator #(.width(3)) comparator_3 (.a(MEM_WB_RegRd), .b(ID_EX_RegRt), .eq(comparator_3_eq));  // open: gt, lt
  and and_3 (ForwardB[0], ~comparator_2_eq, comparator_3_eq, ~comparator_5_eq, MEM_WB_RegWrite);  // AND_Gate
  Comparator #(.width(3)) comparator_4 (.a(EX_MEM_RegRd), .b(3'b000), .eq(comparator_4_eq));  // open: gt, lt
  Comparator #(.width(3)) comparator_5 (.a(3'b000), .b(MEM_WB_RegRd), .eq(comparator_5_eq));  // open: gt, lt
  Comparator #(.width(3)) comparator_6 (.a(MEM_WB_RegRd), .b(ID_EX_RegRs), .eq(comparator_6_eq));  // open: gt, lt
  and and_4 (ForwardA[0], ~comparator_1_eq, comparator_6_eq, ~comparator_5_eq, MEM_WB_RegWrite);  // AND_Gate
endmodule

module Hazard (
  input  ID_EX_MemRead,
  input  [2:0] ID_EX_RegRt,
  input  [2:0] IF_ID_RegRs,
  input  [2:0] IF_ID_RegRt,
  output Stall
);

  wire comparator_1_eq, comparator_2_eq, or_1_out;

  Comparator #(.width(3)) comparator_1 (.a(ID_EX_RegRt), .b(IF_ID_RegRs), .eq(comparator_1_eq));  // open: gt, lt
  Comparator #(.width(3)) comparator_2 (.a(ID_EX_RegRt), .b(IF_ID_RegRt), .eq(comparator_2_eq));  // open: gt, lt
  or or_1 (or_1_out, comparator_1_eq, comparator_2_eq);
  and and_1 (Stall, ID_EX_MemRead, or_1_out);
endmodule

module Meomry (
  input  [15:0] Data_IN,
  input  [15:0] Address,
  input  Memory_Read,
  input  Memory_Write,
  input  CLK,
  input  CLR,
  output [15:0] Data_OUT
);

  wire not_1_out, not_2_out, or_1_out;
  wire [15:0] ram_1_data;

  or or_1 (or_1_out, Memory_Read, Memory_Write);
  RAM #(.addrWidth(16), .dataWidth(16)) ram_1 (
    .addr(Address), .data(ram_1_data), .sel(or_1_out), .clk(CLK), .ld(not_1_out), .clr(CLR));
  not not_1 (not_1_out, Memory_Write);
  assign ram_1_data = Memory_Write ? Data_IN : 16'bz;  // Controlled_Buffer controlled_buffer_1
  assign Data_OUT = not_2_out ? ram_1_data : 16'bz;  // Controlled_Buffer controlled_buffer_2
  not not_2 (not_2_out, Memory_Write);
endmodule

module Control (
  input  [15:0] Instructions,
  output [1:0] RegDes,
  output RegWrite,
  output ExtOp,
  output ALU_Src,
  output Beq,
  output J,
  output MemRead,
  output MemWrite,
  output MemtoReg,
  output [11:0] Immediate,
  output SB,
  output JAL,
  output LUI,
  output LB,
  output LBU,
  output JR,
  output [2:0] Rd,
  output [2:0] Rt,
  output [2:0] Rs,
  output [2:0] ALU_Control
);

  wire ADDI, ANDI, I_Type, J_t, J_Type, LW, LWS_out, not_1_out, or_1_out, or_2_out, or_14_out, ORI, R_Type,
       SW;
  wire [2:0] or_5_out;
  wire [5:0] bit_extender_1_out, multiplexer_1_out;
  wire [11:0] bit_extender_2_out;

  or or_1 (or_1_out, R_Type, I_Type);
  assign bit_extender_1_out = {{5{1'b0}}, 1'b0};  // Bit_Extender bit_extender_1
  or or_2 (or_2_out, J_Type, I_Type);
  Multiplexer #(.width(6), .enable("false")) multiplexer_1 (
    .in0(bit_extender_1_out), .in1(Instructions[11:6]), .out(multiplexer_1_out), .sel(J_Type));
  not not_1 (not_1_out, or_2_out);
  assign Rd = not_1_out ? Instructions[5:3] : 3'bz;  // Controlled_Buffer controlled_buffer_1
  assign bit_extender_2_out = {{11{1'b0}}, R_Type};  // Bit_Extender bit_extender_2
  assign Rt = or_1_out ? Instructions[8:6] : 3'bz;  // Controlled_Buffer controlled_buffer_2
  assign Rs = or_1_out ? Instructions[11:9] : 3'bz;  // Controlled_Buffer controlled_buffer_3
  assign Immediate = ~bit_extender_2_out & {multiplexer_1_out, Instructions[5:0]};  // AND_Gate and_1, 12 bits wide
  and and_2 (R_Type, ~Instructions[12], ~Instructions[13], ~Instructions[14], ~Instructions[15]);  // AND_Gate
  and u_ANDI (ANDI, Instructions[12], ~Instructions[13], ~Instructions[14], ~Instructions[15]);  // AND_Gate
  and u_ORI (ORI, ~Instructions[12], Instructions[13], ~Instructions[14], ~Instructions[15]);  // AND_Gate
  and u_ADDI (ADDI, Instructions[12], Instructions[13], ~Instructions[14], ~Instructions[15]);  // AND_Gate
  and u_LW (LW, ~Instructions[12], ~Instructions[13], Instructions[14], ~Instructions[15]);  // AND_Gate
  and u_LBU (LBU, Instructions[12], ~Instructions[13], Instructions[14], ~Instructions[15]);  // AND_Gate
  and u_LB (LB, ~Instructions[12], Instructions[13], Instructions[14], ~Instructions[15]);  // AND_Gate
  and u_LUI (LUI, ~Instructions[12], ~Instructions[13], Instructions[14], Instructions[15]);  // AND_Gate
  and u_SW (SW, Instructions[12], Instructions[13], Instructions[14], ~Instructions[15]);  // AND_Gate
  and u_SB (SB, ~Instructions[12], ~Instructions[13], ~Instructions[14], Instructions[15]);  // AND_Gate
  and u_BEQ (Beq, Instructions[12], ~Instructions[13], ~Instructions[14], Instructions[15]);  // AND_Gate
  and u_J (J_t, ~Instructions[12], Instructions[13], ~Instructions[14], Instructions[15]);  // AND_Gate
  and u_JAL (JAL, Instructions[12], Instructions[13], ~Instructions[14], Instructions[15]);  // AND_Gate
  and LWS (LWS_out, ~Instructions[0], ~Instructions[1], Instructions[2], ~Instructions[12], ~Instructions[13], ~Instructions[14], ~Instructions[15]);  // AND_Gate
  or or_3 (or_5_out[2], ANDI, ORI);
  or or_4 (I_Type, LBU, LB, LW, SB, ANDI, Beq, SW, ADDI, ORI);
  or or_5 (or_5_out[0], LBU, LB, LW, SB, ANDI, SW, ADDI);
  or or_6 (J_Type, JAL, J_t, LUI);
  or or_7 (RegWrite, R_Type, ANDI, ORI, ADDI, LW, LBU, LB, LUI);
  or or_8 (ExtOp, ADDI, LW, LB, SW, SB);
  or or_9 (ALU_Src, ANDI, ORI, ADDI, LW, LBU, LB, SW, SB);
  or or_10 (J, J_t, JAL, LUI);
  or or_11 (MemRead, LWS_out, LW, LBU, LB);
  or or_12 (MemWrite, SW, SB);
  or or_13 (MemtoReg, LW, LBU, LB);
  Multiplexer #(.width(3), .enable("false")) multiplexer_2 (
    .in0(Instructions[2:0]), .in1({or_5_out[2], I_Type, or_5_out[0]}), .out(ALU_Control), .sel(or_14_out));
  or or_14 (or_14_out, Instructions[12], Instructions[13], Instructions[14], Instructions[15]);
  Multiplexer #(.enable("false")) multiplexer_3 (.in0(LUI), .in1(R_Type), .out(RegDes[0]), .sel(R_Type));
  Multiplexer #(.enable("false")) multiplexer_4 (.in0(JAL), .in1(LUI), .out(RegDes[1]), .sel(RegDes[0]));
  nor nor_1 (JR, Instructions[12], Instructions[13], Instructions[14], Instructions[15], Instructions[0], Instructions[1], Instructions[2]);

  // Other names for the same wires on the sheet: opcode[3:0] = Instructions[15:12]

  // Notes on the sheet:
  //   Function
  //   R-type
endmodule

module DataPath (
  output [15:0] out_1,
  output [2:0] out_2,
  output [2:0] out_3,
  output [2:0] out_4
);

  wire alu_1_zeroflag, AluSrc, clock_1_out, Ex_AluSrc, Ex_BEQ, Ex_ExtOp, Ex_J, Ex_JAL, Ex_JR, Ex_LB, Ex_LBU,
       Ex_LUI, Ex_MemRead, Ex_MemToReg, Ex_MemWrite, Ex_RegWrite, Ex_SB, J, JR, Mem_BEQ, Mem_EXtOP, Mem_J,
       Mem_JAL, Mem_LB, Mem_LBU, Mem_LUI, Mem_MemRead, Mem_MemToReg, Mem_MemWrite, Mem_RegWrite, Mem_SB,
       multiplexer_2_out, not_1_out, not_2_out, or_1_out, PCSrc, register_2_q, Stall,
       wb_buffer_1_wb_memtoreg, WB_ExtOP, WB_JAL, WB_LB, WB_LBU, WB_LUI, WB_RegWrite;
  wire [0:0] not_3_out;
  wire [1:0] Ex_RegDest, ForwardA, ForwardB, Mem_RegDest, multiplexer_4_out, RegDest, selectpc_1_bit0,
       WB_RegDest;
  wire [2:0] Ex_Rd, Ex_Rs, Ex_Rt, Instruction_alu_control, Instruction_rd, Mem_ChoosenReg, Mem_Rd,
       multiplexer_4_out_3, multiplexer_5_out, WB_choosenReg, WB_RegRd;
  wire [7:0] multiplexer_12_out;
  wire [10:0] Instruction_immediate;
  wire [11:11] Instruction_immediate_2;
  wire [15:0] adder_3_out, bit_extender_1_out, bit_extender_2_out, bit_extender_3_out, bit_extender_4_out,
       Ex_PC_1, exec_buffer_1_busa_2, exec_buffer_1_busb_2, exec_buffer_1_imm_out, fetch_buffer_1_ir_out,
       mem_buffer_1_alu_out_2, Mem_imm, Mem_PC_1, meomry_1_data_out, multiplexer_1_out, multiplexer_3_out,
       multiplexer_6_out, multiplexer_7_out, multiplexer_8_out, multiplexer_9_out, multiplexer_10_out,
       multiplexer_11_out, PC_1, pc_1_t, PC_IMM, PC_q, register_1_bus_b, rom_1_data, RS, shifter_1_out,
       shifter_2_out, wb_buffer_1_wb_address, wb_buffer_1_wb_memout, WB_imm, WB_PC_1;
  wire [15:2] Instruction_extop, multiplexer_4_out_2;
  wire [15:8] multiplexer_12_out_2;

  SelectPC selectpc_1 (
    .JR(JR), .JAL(WB_JAL), .J(J), .PCsrc(PCSrc), .Bit0(selectpc_1_bit0[0]), .Bit1(selectpc_1_bit0[1]));
  Multiplexer #(.select(2), .width(16), .enable("false")) multiplexer_1 (
    .in0(PC_1), .in1(adder_3_out), .in2(PC_IMM), .in3(RS), .out(multiplexer_1_out), .sel(selectpc_1_bit0));
  not not_1 (not_1_out, Stall);
  Clock clock_1 (.out(clock_1_out));
  Register_part #(.width(16)) PC (.D(multiplexer_1_out), .en(not_1_out), .Q(PC_q), .clk(clock_1_out));  // open: clr
  Adder #(.width(16)) adder_1 (.a(PC_q), .b(bit_extender_1_out), .out(PC_IMM));  // open: cin, cout
  Adder #(.width(16)) adder_2 (.a(PC_q), .b(16'h1), .out(PC_1));  // open: cin, cout
  ROM #(.addrWidth(16), .dataWidth(16)) rom_1 (.addr(PC_q), .data(rom_1_data));  // open: sel
  not not_2 (not_2_out, Stall);
  Fetch_buffer fetch_buffer_1 (
    .PC_1_in(PC_1), .IR_in(rom_1_data), .CLK(clock_1_out), .EN(not_2_out), .PC_1_out(pc_1_t),
    .IR_out(fetch_buffer_1_ir_out));  // open: CLR
  Multiplexer #(.enable("false")) multiplexer_2 (
    .in0(1'b0), .in1(Instruction_immediate_2[11]), .out(multiplexer_2_out), .sel(Instruction_extop[2]));
  Hazard Hazard (
    .ID_EX_MemRead(Ex_MemRead), .ID_EX_RegRt(Ex_Rt), .IF_ID_RegRs(out_2), .IF_ID_RegRt(out_3), .Stall(Stall));
  Control Instruction (
    .Instructions(fetch_buffer_1_ir_out), .RegDes(RegDest), .RegWrite(Instruction_extop[3]),
    .ExtOp(Instruction_extop[2]), .ALU_Src(AluSrc), .Beq(Instruction_extop[8]), .J(J),
    .MemRead(Instruction_extop[5]), .MemWrite(Instruction_extop[6]), .MemtoReg(Instruction_extop[7]),
    .Immediate({Instruction_immediate_2[11], Instruction_immediate}), .SB(Instruction_extop[10]),
    .Rd(Instruction_rd), .Rt(out_3), .Rs(out_2), .ALU_Control(Instruction_alu_control),
    .JAL(Instruction_extop[12]), .JR(JR), .LUI(Instruction_extop[13]), .LB(Instruction_extop[15]),
    .LBU(Instruction_extop[14]));
  assign bit_extender_1_out = {{4{multiplexer_2_out}}, {Instruction_immediate_2[11], Instruction_immediate}};  // Bit_Extender bit_extender_1
  Shifter #(.width(16)) shifter_1 (.in(bit_extender_1_out), .\dist (4'b0100), .out(shifter_1_out));
  Shifter #(.width(16)) shifter_2 (.in(exec_buffer_1_imm_out), .\dist (4'b0010), .out(shifter_2_out));
  Multiplexer #(.select(2), .width(16), .enable("false")) multiplexer_3 (
    .in0(WB_PC_1), .in1(multiplexer_11_out), .in2(shifter_1_out), .out(multiplexer_3_out),
    .sel({WB_LUI, not_3_out[0]}));  // open: in3
  not not_3 (not_3_out[0], WB_JAL);
  Adder #(.width(16)) adder_3 (.a(PC_1), .b(shifter_2_out), .out(adder_3_out));  // open: cin, cout
  Multiplexer #(.width(19), .enable("false")) multiplexer_4 (
    .in0({Instruction_alu_control, Instruction_extop[15:12], JR, Instruction_extop[10], J, Instruction_extop[8:5], AluSrc, Instruction_extop[3:2], RegDest}),
    .in1({19{1'b0}}), .out({multiplexer_4_out_3, multiplexer_4_out_2, multiplexer_4_out}), .sel(Stall));
  Register register_1 (
    .WR_en(WB_RegWrite), .Decoder_sel(WB_choosenReg), .BUS_W(multiplexer_3_out), .RA(out_2), .RB(out_3),
    .CLK(clock_1_out), .BUS_A(RS), .BUS_B(register_1_bus_b));
  Exec_buffer exec_buffer_1 (
    .IMM_in(bit_extender_1_out), .BusA(RS), .PC_1_in(PC_1), .Rd_in(Instruction_rd), .Rs_in(out_2),
    .BusB(register_1_bus_b), .Rt_in(out_3), .CLK(clock_1_out), .IMM_out(exec_buffer_1_imm_out),
    .BusA_2(exec_buffer_1_busa_2), .PC_1_out(Ex_PC_1), .Rd_out(Ex_Rd), .Rs_out(Ex_Rs),
    .BusB_2(exec_buffer_1_busb_2), .Rt_out(Ex_Rt), .Fetch_J(multiplexer_4_out_2[9]), .Exe_j(Ex_J),
    .Fetch_BEQ(multiplexer_4_out_2[8]), .Exe_BEQ(Ex_BEQ), .Fetch_RegWrite(multiplexer_4_out_2[2]),
    .Exe_RegWrite(Ex_RegWrite), .Fetch_MemWrite(multiplexer_4_out_2[6]), .Exe_MemWrite(Ex_MemWrite),
    .Fetch_MemToReg(multiplexer_4_out_2[7]), .Exe_MemToReg(Ex_MemToReg),
    .Fetch_MemRead(multiplexer_4_out_2[5]), .Exe_MemRead(Ex_MemRead), .Fetch_LUI(multiplexer_4_out_2[13]),
    .Exe_LUI(Ex_LUI), .Fetch_RegDest(multiplexer_4_out), .Exe_RegDest(Ex_RegDest),
    .Fetch_ExtOP(multiplexer_4_out_2[3]), .Exe_ExtOP(Ex_ExtOp), .Fetch_SB(multiplexer_4_out_2[10]),
    .Exe_SB(Ex_SB), .Fetch_JR(multiplexer_4_out_2[11]), .Exe_JR(Ex_JR), .Fetch_JAL(multiplexer_4_out_2[12]),
    .Exe_JAL(Ex_JAL), .Fetch_LBU(multiplexer_4_out_2[14]), .Exe_LBU(Ex_LBU),
    .Fetch_LB(multiplexer_4_out_2[15]), .Exe_LB(Ex_LB), .Fetch_AluCtrl(multiplexer_4_out_3),
    .Exe_AluCtrl(out_4), .Fetch_AluSrc(multiplexer_4_out_2[4]), .Exe_ALuSrc(Ex_AluSrc));
  Multiplexer #(.select(2), .width(3), .enable("false")) multiplexer_5 (
    .in0(Ex_Rt), .in1(Ex_Rd), .in2(3'b111), .in3(3'b001), .out(multiplexer_5_out), .sel(Ex_RegDest));
  Multiplexer #(.width(16), .enable("false")) multiplexer_6 (
    .in0(exec_buffer_1_busb_2), .in1(exec_buffer_1_imm_out), .out(multiplexer_6_out), .sel(Ex_AluSrc));
  Multiplexer #(.select(2), .width(16), .enable("false")) multiplexer_7 (
    .in0(exec_buffer_1_busa_2), .in1(multiplexer_11_out), .in2(out_1), .out(multiplexer_7_out), .sel(ForwardA));  // open: in3
  Multiplexer #(.select(2), .width(16), .enable("false")) multiplexer_8 (
    .in0(multiplexer_6_out), .in1(multiplexer_11_out), .in2(out_1), .out(multiplexer_8_out), .sel(ForwardB));  // open: in3
  Forwarding forwarding_1 (
    .ForwardA(ForwardA), .ForwardB(ForwardB), .EX_MEM_RegRd(Mem_Rd), .ID_EX_RegRs(Ex_Rs),
    .ID_EX_RegRt(Ex_Rt), .EX_MEM_RegWrite(Mem_RegWrite), .MEM_WB_RegWrite(WB_RegWrite),
    .MEM_WB_RegRd(WB_RegRd));
  ALU alu_1 (
    .A(multiplexer_7_out), .B(multiplexer_8_out), .Alu_OP(out_4), .\output (out_1),
    .ZeroFlag(alu_1_zeroflag), .in_4(1'b1));  // open: carry_out
  assign bit_extender_2_out = {{8{exec_buffer_1_imm_out[7]}}, exec_buffer_1_imm_out[7:0]};  // Bit_Extender bit_extender_2
  Multiplexer #(.width(16), .enable("false")) multiplexer_9 (
    .in0(exec_buffer_1_imm_out), .in1(bit_extender_2_out), .out(multiplexer_9_out), .sel(Mem_SB));
  Register_part #(.width(1)) register_2 (
    .D(alu_1_zeroflag), .en(1'b1), .Q(register_2_q), .clk(clock_1_out));  // open: clr
  Multiplexer #(.width(16), .enable("false")) multiplexer_10 (
    .in0(bit_extender_4_out), .in1(bit_extender_3_out), .out(multiplexer_10_out), .sel(WB_LBU));
  Mem_buffer mem_buffer_1 (
    .PC_1(PC_1), .PC_1_2(Mem_PC_1), .choosenReg(multiplexer_5_out), .Mem_choosenReg(Mem_ChoosenReg),
    .ALu_out(out_1), .Alu_out_2(mem_buffer_1_alu_out_2), .J(Ex_J), .Mem_J(Mem_J), .BEQ(Ex_BEQ),
    .Mem_BEQ(Mem_BEQ), .RegWrite(Ex_RegWrite), .Mem_RegWrite(Mem_RegWrite), .MemWrite(Ex_MemWrite),
    .Mem_MemWrite(Mem_MemWrite), .MemToReg(Ex_MemToReg), .Mem_MemToReg(Mem_MemToReg), .MemRead(Ex_MemRead),
    .Mem_MemRead(Mem_MemRead), .Ex_RegRd(Ex_Rd), .Mem_RegRd(Mem_Rd), .CLK(clock_1_out), .JAL(Ex_JAL),
    .Mem_JAL(Mem_JAL), .RegDest(Ex_RegDest), .Mem_RegDest(Mem_RegDest), .LUI(Ex_LUI), .Mem_LUI(Mem_LUI),
    .SB(Ex_SB), .Mem_SB(Mem_SB), .LB(Ex_LB), .Mem_LB(Mem_LB), .LBU(Ex_LBU), .Mem_LBU(Mem_LBU),
    .ExtOP(Ex_ExtOp), .Mem_ExtOP(Mem_EXtOP), .imm(exec_buffer_1_imm_out), .imm_2(Mem_imm));  // open: CLR
  Meomry meomry_1 (
    .Data_IN(multiplexer_9_out), .Address(mem_buffer_1_alu_out_2), .CLK(clock_1_out),
    .Data_OUT(meomry_1_data_out), .Memory_Read(Mem_MemRead), .Memory_Write(Mem_MemWrite));  // open: CLR
  Multiplexer #(.width(16), .enable("false")) multiplexer_11 (
    .in0({multiplexer_12_out_2, multiplexer_12_out}), .in1(multiplexer_10_out), .out(multiplexer_11_out),
    .sel(or_1_out));
  or or_1 (or_1_out, WB_LB, WB_LBU);
  Pcbeq pcbeq_1 (.PCsrc(PCSrc), .Zero(register_2_q), .BEQ(Mem_BEQ));
  assign bit_extender_3_out = {{8{1'b0}}, multiplexer_12_out};  // Bit_Extender bit_extender_3
  assign bit_extender_4_out = {{8{multiplexer_12_out[7]}}, multiplexer_12_out};  // Bit_Extender bit_extender_4
  WB_buffer wb_buffer_1 (
    .Mem_Address(mem_buffer_1_alu_out_2), .Mem_out(meomry_1_data_out), .Mem_MemToReg(Mem_MemToReg),
    .Mem_RegWrite(Mem_RegWrite), .Mem_RegDest(Mem_RegDest), .LUI(Mem_LUI), .CLK(clock_1_out),
    .WB_Address(wb_buffer_1_wb_address), .WB_MemOut(wb_buffer_1_wb_memout),
    .WB_MemToReg(wb_buffer_1_wb_memtoreg), .WB_RegWrite(WB_RegWrite), .WB_RegDest(WB_RegDest),
    .WB_LUI(WB_LUI), .Mem_RegRd(Mem_Rd), .WB_RegRd(WB_RegRd), .Mem_imm(Mem_imm), .WB_imm(WB_imm),
    .Mem_pc_1(Mem_PC_1), .WB_pc_1(WB_PC_1), .Mem_ExtOP(Mem_EXtOP), .WB_EXtOp(WB_ExtOP), .LB(Mem_LB),
    .WB_LB(WB_LB), .LBU(Mem_LBU), .WB_LBU(WB_LBU), .JAL(Mem_JAL), .JAL_2(WB_JAL),
    .Mem_ChoosenReg(Mem_ChoosenReg), .WB_ChoosenReg(WB_choosenReg));  // open: CLR
  Multiplexer #(.width(16), .enable("false")) multiplexer_12 (
    .in0(wb_buffer_1_wb_address), .in1(wb_buffer_1_wb_memout),
    .out({multiplexer_12_out_2, multiplexer_12_out}), .sel(wb_buffer_1_wb_memtoreg));

  // Other names for the same wires on the sheet: Ex_ALUCtrl[2:0] = out_4

  // Notes on the sheet:
  //   contents of rom_1 (hex, n*v repeats v):
  //   5441 15*1
  //   BTA
endmodule

// IF/Dec buffer
module Fetch_buffer (
  input  [15:0] PC_1_in,
  input  [15:0] IR_in,
  input  CLK,
  input  CLR,
  input  EN,
  output [15:0] PC_1_out,
  output [15:0] IR_out
);

  wire undriven;

  Register_part #(.width(16), .trigger("falling")) register_1 (
    .D(PC_1_in), .en(EN), .Q(PC_1_out), .clk(CLK), .clr(undriven));
  Register_part #(.width(16), .trigger("falling")) register_2 (.D(IR_in), .en(EN), .Q(IR_out), .clk(CLK), .clr(CLR));
endmodule

// Dec/Exec buffer
module Exec_buffer (
  input  Fetch_AluSrc,
  input  [1:0] Fetch_RegDest,
  input  Fetch_ExtOP,
  input  Fetch_SB,
  input  Fetch_JR,
  input  Fetch_JAL,
  input  Fetch_LUI,
  input  Fetch_LBU,
  input  Fetch_LB,
  input  [2:0] Fetch_AluCtrl,
  input  [15:0] IMM_in,
  input  [15:0] BusA,
  input  [15:0] PC_1_in,
  input  [2:0] Rd_in,
  input  [2:0] Rs_in,
  input  [15:0] BusB,
  input  [2:0] Rt_in,
  input  Fetch_J,
  input  Fetch_BEQ,
  input  Fetch_RegWrite,
  input  Fetch_MemWrite,
  input  Fetch_MemToReg,
  input  Fetch_MemRead,
  input  CLK,
  output Exe_ALuSrc,
  output [1:0] Exe_RegDest,
  output Exe_ExtOP,
  output Exe_SB,
  output Exe_JR,
  output Exe_JAL,
  output Exe_LUI,
  output Exe_LBU,
  output Exe_LB,
  output [2:0] Exe_AluCtrl,
  output [15:0] IMM_out,
  output [15:0] BusA_2,
  output [15:0] PC_1_out,
  output [2:0] Rd_out,
  output [2:0] Rs_out,
  output [15:0] BusB_2,
  output [2:0] Rt_out,
  output Exe_j,
  output Exe_BEQ,
  output Exe_RegWrite,
  output Exe_MemWrite,
  output Exe_MemToReg,
  output Exe_MemRead
);

  Register_part #(.width(1), .trigger("falling")) register_1 (
    .D(Fetch_AluSrc), .en(1'b1), .Q(Exe_ALuSrc), .clk(CLK), .clr(1'b0));
  Register_part #(.width(2), .trigger("falling")) register_2 (
    .D(Fetch_RegDest), .en(1'b1), .Q(Exe_RegDest), .clk(CLK), .clr(1'b0));
  Register_part #(.width(1), .trigger("falling")) register_3 (
    .D(Fetch_ExtOP), .en(1'b1), .Q(Exe_ExtOP), .clk(CLK), .clr(1'b0));
  Register_part #(.width(1), .trigger("falling")) register_4 (
    .D(Fetch_SB), .en(1'b1), .Q(Exe_SB), .clk(CLK), .clr(1'b0));
  Register_part #(.width(1), .trigger("falling")) register_5 (
    .D(Fetch_JR), .en(1'b1), .Q(Exe_JR), .clk(CLK), .clr(1'b0));
  Register_part #(.width(1), .trigger("falling")) register_6 (
    .D(Fetch_JAL), .en(1'b1), .Q(Exe_JAL), .clk(CLK), .clr(1'b0));
  Register_part #(.width(1), .trigger("falling")) register_7 (
    .D(Fetch_LUI), .en(1'b1), .Q(Exe_LUI), .clk(CLK), .clr(1'b0));
  Register_part #(.width(1), .trigger("falling")) register_8 (
    .D(Fetch_LBU), .en(1'b1), .Q(Exe_LBU), .clk(CLK), .clr(1'b0));
  Register_part #(.width(1), .trigger("falling")) register_9 (
    .D(Fetch_LB), .en(1'b1), .Q(Exe_LB), .clk(CLK), .clr(1'b0));
  Register_part #(.width(3), .trigger("falling")) register_10 (
    .D(Fetch_AluCtrl), .en(1'b1), .Q(Exe_AluCtrl), .clk(CLK), .clr(1'b0));
  Register_part #(.width(16), .trigger("falling")) register_11 (
    .D(IMM_in), .en(1'b1), .Q(IMM_out), .clk(CLK), .clr(1'b0));
  Register_part #(.width(16), .trigger("falling")) register_12 (.D(BusA), .en(1'b1), .Q(BusA_2), .clk(CLK), .clr(1'b0));
  Register_part #(.width(16), .trigger("falling")) register_13 (
    .D(PC_1_in), .en(1'b1), .Q(PC_1_out), .clk(CLK), .clr(1'b0));
  Register_part #(.width(3), .trigger("falling")) register_14 (.D(Rd_in), .en(1'b1), .Q(Rd_out), .clk(CLK), .clr(1'b0));
  Register_part #(.width(3), .trigger("falling")) register_15 (.D(Rs_in), .en(1'b1), .Q(Rs_out), .clk(CLK), .clr(1'b0));
  Register_part #(.width(16), .trigger("falling")) register_16 (.D(BusB), .en(1'b1), .Q(BusB_2), .clk(CLK), .clr(1'b0));
  Register_part #(.width(3), .trigger("falling")) register_17 (.D(Rt_in), .en(1'b1), .Q(Rt_out), .clk(CLK), .clr(1'b0));
  Register_part #(.width(1), .trigger("falling")) register_18 (
    .D(Fetch_J), .en(1'b1), .Q(Exe_j), .clk(CLK), .clr(1'b0));
  Register_part #(.width(1), .trigger("falling")) register_19 (
    .D(Fetch_BEQ), .en(1'b1), .Q(Exe_BEQ), .clk(CLK), .clr(1'b0));
  Register_part #(.width(1), .trigger("falling")) register_20 (
    .D(Fetch_RegWrite), .en(1'b1), .Q(Exe_RegWrite), .clk(CLK), .clr(1'b0));
  Register_part #(.width(1), .trigger("falling")) register_21 (
    .D(Fetch_MemWrite), .en(1'b1), .Q(Exe_MemWrite), .clk(CLK), .clr(1'b0));
  Register_part #(.width(1), .trigger("falling")) register_22 (
    .D(Fetch_MemToReg), .en(1'b1), .Q(Exe_MemToReg), .clk(CLK), .clr(1'b0));
  Register_part #(.width(1), .trigger("falling")) register_23 (
    .D(Fetch_MemRead), .en(1'b1), .Q(Exe_MemRead), .clk(CLK), .clr(1'b0));

  // Notes on the sheet:
  //   Decode/Execute
endmodule

module Pcbeq (
  input  Zero,
  input  BEQ,
  output PCsrc
);

  and and_1 (PCsrc, Zero, BEQ);
endmodule

// Exec/Mem buffer
module Mem_buffer (
  input  JAL,
  input  [1:0] RegDest,
  input  LUI,
  input  [15:0] imm,
  input  SB,
  input  LB,
  input  LBU,
  input  ExtOP,
  input  [15:0] PC_1,
  input  [2:0] choosenReg,
  input  [15:0] ALu_out,
  input  J,
  input  BEQ,
  input  RegWrite,
  input  MemWrite,
  input  MemToReg,
  input  MemRead,
  input  [2:0] Ex_RegRd,
  input  CLK,
  input  CLR,
  output Mem_JAL,
  output [1:0] Mem_RegDest,
  output Mem_LUI,
  output [15:0] imm_2,
  output Mem_SB,
  output Mem_LB,
  output Mem_LBU,
  output Mem_ExtOP,
  output [15:0] PC_1_2,
  output [2:0] Mem_choosenReg,
  output [15:0] Alu_out_2,
  output Mem_J,
  output Mem_BEQ,
  output Mem_RegWrite,
  output Mem_MemWrite,
  output Mem_MemToReg,
  output Mem_MemRead,
  output [2:0] Mem_RegRd
);

  Register_part #(.width(1), .trigger("falling")) register_1 (.D(JAL), .en(1'b1), .Q(Mem_JAL), .clk(CLK), .clr(CLR));
  Register_part #(.width(2), .trigger("falling")) register_2 (
    .D(RegDest), .en(1'b1), .Q(Mem_RegDest), .clk(CLK), .clr(CLR));
  Register_part #(.width(1), .trigger("falling")) register_3 (.D(LUI), .en(1'b1), .Q(Mem_LUI), .clk(CLK), .clr(CLR));
  Register_part #(.width(16), .trigger("falling")) register_4 (.D(imm), .en(1'b1), .Q(imm_2), .clk(CLK), .clr(CLR));
  Register_part #(.width(1), .trigger("falling")) register_5 (.D(SB), .en(1'b1), .Q(Mem_SB), .clk(CLK), .clr(CLR));
  Register_part #(.width(1), .trigger("falling")) register_6 (.D(LB), .en(1'b1), .Q(Mem_LB), .clk(CLK), .clr(CLR));
  Register_part #(.width(1), .trigger("falling")) register_7 (.D(LBU), .en(1'b1), .Q(Mem_LBU), .clk(CLK), .clr(CLR));
  Register_part #(.width(1), .trigger("falling")) register_8 (
    .D(ExtOP), .en(1'b1), .Q(Mem_ExtOP), .clk(CLK), .clr(CLR));
  Register_part #(.width(16), .trigger("falling")) register_9 (.D(PC_1), .en(1'b1), .Q(PC_1_2), .clk(CLK), .clr(CLR));
  Register_part #(.width(3), .trigger("falling")) register_10 (
    .D(choosenReg), .en(1'b1), .Q(Mem_choosenReg), .clk(CLK), .clr(CLR));
  Register_part #(.width(16), .trigger("falling")) register_11 (
    .D(ALu_out), .en(1'b1), .Q(Alu_out_2), .clk(CLK), .clr(CLR));
  Register_part #(.width(1), .trigger("falling")) register_12 (.D(J), .en(1'b1), .Q(Mem_J), .clk(CLK), .clr(CLR));
  Register_part #(.width(1), .trigger("falling")) register_13 (.D(BEQ), .en(1'b1), .Q(Mem_BEQ), .clk(CLK), .clr(CLR));
  Register_part #(.width(1), .trigger("falling")) register_14 (
    .D(RegWrite), .en(1'b1), .Q(Mem_RegWrite), .clk(CLK), .clr(CLR));
  Register_part #(.width(1), .trigger("falling")) register_15 (
    .D(MemWrite), .en(1'b1), .Q(Mem_MemWrite), .clk(CLK), .clr(CLR));
  Register_part #(.width(1), .trigger("falling")) register_16 (
    .D(MemToReg), .en(1'b1), .Q(Mem_MemToReg), .clk(CLK), .clr(CLR));
  Register_part #(.width(1), .trigger("falling")) register_17 (
    .D(MemRead), .en(1'b1), .Q(Mem_MemRead), .clk(CLK), .clr(CLR));
  Register_part #(.width(3), .trigger("falling")) register_18 (
    .D(Ex_RegRd), .en(1'b1), .Q(Mem_RegRd), .clk(CLK), .clr(CLR));

  // Notes on the sheet:
  //   Execute/Memory
endmodule

// Mem/WB buffer
module WB_buffer (
  input  [15:0] Mem_Address,
  input  [15:0] Mem_out,
  input  Mem_MemToReg,
  input  Mem_RegWrite,
  input  [1:0] Mem_RegDest,
  input  LUI,
  input  [2:0] Mem_RegRd,
  input  [15:0] Mem_imm,
  input  [15:0] Mem_pc_1,
  input  Mem_ExtOP,
  input  LB,
  input  LBU,
  input  JAL,
  input  [2:0] Mem_ChoosenReg,
  input  CLK,
  input  CLR,
  output [15:0] WB_Address,
  output [15:0] WB_MemOut,
  output WB_MemToReg,
  output WB_RegWrite,
  output [1:0] WB_RegDest,
  output WB_LUI,
  output [2:0] WB_RegRd,
  output [15:0] WB_imm,
  output [15:0] WB_pc_1,
  output WB_EXtOp,
  output WB_LB,
  output WB_LBU,
  output JAL_2,
  output [2:0] WB_ChoosenReg
);

  Register_part #(.width(16), .trigger("falling")) register_1 (
    .D(Mem_Address), .en(1'b1), .Q(WB_Address), .clk(CLK), .clr(CLR));
  Register_part #(.width(16), .trigger("falling")) register_2 (
    .D(Mem_out), .en(1'b1), .Q(WB_MemOut), .clk(CLK), .clr(CLR));
  Register_part #(.width(1), .trigger("falling")) register_3 (
    .D(Mem_MemToReg), .en(1'b1), .Q(WB_MemToReg), .clk(CLK), .clr(CLR));
  Register_part #(.width(1), .trigger("falling")) register_4 (
    .D(Mem_RegWrite), .en(1'b1), .Q(WB_RegWrite), .clk(CLK), .clr(CLR));
  Register_part #(.width(2), .trigger("falling")) register_5 (
    .D(Mem_RegDest), .en(1'b1), .Q(WB_RegDest), .clk(CLK), .clr(CLR));
  Register_part #(.width(1), .trigger("falling")) register_6 (.D(LUI), .en(1'b1), .Q(WB_LUI), .clk(CLK), .clr(CLR));
  Register_part #(.width(3), .trigger("falling")) register_7 (
    .D(Mem_RegRd), .en(1'b1), .Q(WB_RegRd), .clk(CLK), .clr(CLR));
  Register_part #(.width(16), .trigger("falling")) register_8 (
    .D(Mem_imm), .en(1'b1), .Q(WB_imm), .clk(CLK), .clr(CLR));
  Register_part #(.width(16), .trigger("falling")) register_9 (
    .D(Mem_pc_1), .en(1'b1), .Q(WB_pc_1), .clk(CLK), .clr(CLR));
  Register_part #(.width(1), .trigger("falling")) register_10 (
    .D(Mem_ExtOP), .en(1'b1), .Q(WB_EXtOp), .clk(CLK), .clr(CLR));
  Register_part #(.width(1), .trigger("falling")) register_11 (.D(LB), .en(1'b1), .Q(WB_LB), .clk(CLK), .clr(CLR));
  Register_part #(.width(1), .trigger("falling")) register_12 (.D(LBU), .en(1'b1), .Q(WB_LBU), .clk(CLK), .clr(CLR));
  Register_part #(.width(1), .trigger("falling")) register_13 (.D(JAL), .en(1'b1), .Q(JAL_2), .clk(CLK), .clr(CLR));
  Register_part #(.width(3), .trigger("falling")) register_14 (
    .D(Mem_ChoosenReg), .en(1'b1), .Q(WB_ChoosenReg), .clk(CLK), .clr(CLR));

  // Notes on the sheet:
  //   Memory/WB
endmodule

// PC
module SelectPC (
  input  JR,
  input  JAL,
  input  J,
  input  PCsrc,
  output Bit0,
  output Bit1
);

  wire and_1_out, and_2_out, and_3_out, and_4_out;

  and and_1 (and_1_out, ~JR, JAL, J, ~PCsrc);  // AND_Gate
  and and_2 (and_2_out, JR, ~JAL, ~J, ~PCsrc);  // AND_Gate
  and and_3 (and_3_out, ~JR, ~JAL, ~J, PCsrc);  // AND_Gate
  and and_4 (and_4_out, JR, ~JAL, ~J, ~PCsrc);  // AND_Gate
  or or_1 (Bit0, and_1_out, and_2_out);
  or or_2 (Bit1, and_3_out, and_4_out);
endmodule
